# Fritzing sketch Untitled Sketch (saved by Fritzing 1.0.1rc)
circuit board: 8.46667cm x 5.64444cm
breadboards: 1

parts:
  U1 = atmega328 [package=dip]
  VCC2 = Battery
  R2 = 220 Ω Resistor [package=THT]
  U2 = LCD-16X2 [package=lcd-16x2_noholes]

nets:
  N1: U1.RESET, U1.D11_(PWM), U1.D12, U1.D13, R2.Pin_1
  N2: U1.D2, U2.DB0
  N3: U1.D4, U2.E
  VCC: U1.VCC, VCC2.-, U2.VDD, U2.A
  N4: U1.GND#7, U2.R_W
  N5: U1.D7, U2.DB3
  N6: U1.D8, U2.RS
  GND: U1.GND#21, VCC2.+, U2.VSS, U2.K

custom parts:
  Battery: Your standard 2x AA battery pack (3 Volts)
  220 Ω Resistor: A generic resistor (0.25W)
